# Fritzing sketch Abajur Wifi (saved by Fritzing 0.9.3b)
breadboards: 1

parts:
  WeMos_D1_Mini1 = WeMos D1 Mini
  Q1 = TIP120 Hi-Current Darlington Transistor
  C1 = Electrolytic Capacitor [capacitance=10μF voltage=25V package="0605 [SMD, electrolytic]"]
  R1 = Resistor [tolerance=±5% resistance=1k package="2010 [SMD]"]
  U1 = TRANSISTOR_NPN_2 [package=to-92]
  Power_plug1 = Power plug
  R2 = Resistor [tolerance=±5% resistance=50k package="2010 [SMD]"]
  R3 = Resistor [tolerance=±5% resistance=2k package="2010 [SMD]"]

nets:
  N1: WeMos_D1_Mini1.D2, R1.Pin_0
  N2: Q1.BASE, C1.+, R2.Pin_1, R3.Pin_0
  GND: C1.-, Power_plug1.GND, R2.Pin_0
  N3: R1.Pin_1, U1.B
  N4: U1.C, Power_plug1.VCC
  N5: U1.E, R3.Pin_1
